// Logisim project cpu.circ as structural Verilog: 2 circuits, main circuit main
module main (
  input  [31:0] INSTRUCTION,
  input  CLOCK,
  output [31:0] PROGRAM_COUNTER,
  output [31:0] ra,
  output [31:0] sp,
  output [31:0] t0,
  output [31:0] t1,
  output [31:0] t2,
  output [31:0] s0,
  output [31:0] s1,
  output [31:0] a0
);

  wire ALUB, and_22_out, and_23_out, and_24_out, and_25_out, and_27_out, and_28_out, and_29_out, and_30_out,
       and_31_out, and_32_out, and_33_out, and_34_out, and_35_out, and_36_out, and_37_out, beq_sign,
       blt_sign, bltu_sign, bne_sign, comparator_1_eq, comparator_2_eq, comparator_3_eq, comparator_4_eq,
       comparator_5_eq, comparator_6_eq, comparator_7_eq, comparator_8_eq, comparator_9_eq, comparator_10_eq,
       comparator_11_eq, comparator_12_eq, comparator_13_eq, comparator_17_eq, comparator_18_eq,
       comparator_19_eq, comparator_20_eq, comparator_21_eq, comparator_22_eq, comparator_23_eq,
       comparator_24_eq, comparator_25_eq, comparator_26_eq, comparator_27_eq, comparator_28_eq,
       comparator_29_eq, comparator_30_eq, comparator_31_eq, comparator_32_eq, comparator_33_eq,
       comparator_34_eq, comparator_35_eq, comparator_36_eq, comparator_37_eq, comparator_38_eq,
       comparator_39_eq, comparator_40_eq, comparator_41_eq, comparator_42_eq, comparator_43_eq,
       comparator_44_eq, comparator_45_eq, comparator_46_eq, MemRW, or_3_out, PC_Sel, PC_Sel_tmp, RegWEn,
       RegWEn_IF, store_sel;
  wire [2:0] funct3;
  wire [3:0] ALUSel, ALUSelI, ALUSelR, and_1_out, and_2_out, and_3_out, and_4_out, and_5_out, and_6_out,
       and_7_out, and_8_out, and_9_out, and_10_out, and_11_out, and_12_out, and_13_out, and_14_out,
       and_15_out, and_16_out, and_17_out, and_18_out, and_19_out, and_20_out, and_21_out, and_38_out,
       and_39_out, bit_extender_1_out, bit_extender_2_out, bit_extender_3_out, bit_extender_4_out,
       bit_extender_5_out, bit_extender_6_out, bit_extender_7_out, bit_extender_8_out, bit_extender_9_out,
       bit_extender_10_out, bit_extender_11_out, bit_extender_12_out, bit_extender_13_out,
       bit_extender_14_out, bit_extender_15_out, bit_extender_16_out, bit_extender_17_out,
       bit_extender_18_out, bit_extender_19_out, bit_extender_20_out, bit_extender_21_out,
       bit_extender_22_out, bit_extender_23_out;
  wire [4:0] rd_IF;
  wire [6:0] funct7;
  wire [24:0] INSREUCTION_USE;
  wire [31:0] adder_1_out, adder_2_out, alu_result, immi, immi_USE, multiplexer_1_out, multiplexer_3_out,
       multiplexer_4_out, multiplexer_6_out, multiplexer_7_out, multiplexer_8_out, multiplexer_9_out,
       PC_Result, PROGRAM_COUNTER_EX, Read_data, rs1_output, rs2_output, write_reg;

  imme imme_1 (.out_2(immi), .in_1({funct7, INSREUCTION_USE[24:15], funct3, INSREUCTION_USE[11:0]}));
  Register #(.width(5)) register_1 (.D(INSREUCTION_USE[11:7]), .en(1'b1), .clk(CLOCK), .Q(rd_IF));  // open: clr
  Register #(.width(32)) register_2 (.D(immi), .en(1'b1), .clk(CLOCK), .Q(immi_USE));  // open: clr
  Comparator #(.width(5)) comparator_1 (
    .a({funct3, funct7[5], funct7[0]}), .b(5'b01101), .eq(comparator_1_eq));  // open: gt, lt
  Comparator #(.width(5)) comparator_2 (
    .a({funct3, funct7[5], funct7[0]}), .b({5{1'b0}}), .eq(comparator_2_eq));  // open: gt, lt
  Comparator #(.width(5)) comparator_3 (
    .a({funct3, funct7[5], funct7[0]}), .b(5'b00001), .eq(comparator_3_eq));  // open: gt, lt
  Comparator #(.width(5)) comparator_4 (
    .a({funct3, funct7[5], funct7[0]}), .b(5'b00010), .eq(comparator_4_eq));  // open: gt, lt
  Comparator #(.width(5)) comparator_5 (
    .a({funct3, funct7[5], funct7[0]}), .b(5'b00100), .eq(comparator_5_eq));  // open: gt, lt
  Comparator #(.width(5)) comparator_6 (
    .a({funct3, funct7[5], funct7[0]}), .b(5'b00101), .eq(comparator_6_eq));  // open: gt, lt
  Comparator #(.width(5)) comparator_7 (
    .a({funct3, funct7[5], funct7[0]}), .b(5'b01000), .eq(comparator_7_eq));  // open: gt, lt
  Comparator #(.width(5)) comparator_8 (
    .a({funct3, funct7[5], funct7[0]}), .b(5'b10000), .eq(comparator_8_eq));  // open: gt, lt
  Comparator #(.width(5)) comparator_9 (
    .a({funct3, funct7[5], funct7[0]}), .b(5'b10101), .eq(comparator_9_eq));  // open: gt, lt
  Comparator #(.width(5)) comparator_10 (
    .a({funct3, funct7[5], funct7[0]}), .b(5'b10100), .eq(comparator_10_eq));  // open: gt, lt
  Comparator #(.width(5)) comparator_11 (
    .a({funct3, funct7[5], funct7[0]}), .b(5'b11000), .eq(comparator_11_eq));  // open: gt, lt
  Comparator #(.width(5)) comparator_12 (
    .a({funct3, funct7[5], funct7[0]}), .b(5'b11101), .eq(comparator_12_eq));  // open: gt, lt
  Comparator #(.width(5)) comparator_13 (
    .a({funct3, funct7[5], funct7[0]}), .b(5'b11100), .eq(comparator_13_eq));  // open: gt, lt
  Register #(.width(32)) PC (.D(PC_Result), .en(1'b1), .clk(CLOCK), .Q(PROGRAM_COUNTER));  // open: clr
  Multiplexer #(.width(32), .enable("false")) multiplexer_1 (
    .in0(alu_result), .in1(Read_data), .out(multiplexer_1_out), .sel(store_sel));
  Register #(.width(1)) register_3 (.D(RegWEn), .en(1'b1), .clk(CLOCK), .Q(RegWEn_IF));  // open: clr
  assign bit_extender_1_out = {{3{comparator_1_eq}}, comparator_1_eq};  // Bit_Extender bit_extender_1
  assign bit_extender_2_out = {{3{comparator_2_eq}}, comparator_2_eq};  // Bit_Extender bit_extender_2
  assign bit_extender_3_out = {{3{comparator_3_eq}}, comparator_3_eq};  // Bit_Extender bit_extender_3
  assign bit_extender_4_out = {{3{comparator_4_eq}}, comparator_4_eq};  // Bit_Extender bit_extender_4
  assign bit_extender_5_out = {{3{comparator_5_eq}}, comparator_5_eq};  // Bit_Extender bit_extender_5
  assign bit_extender_6_out = {{3{comparator_6_eq}}, comparator_6_eq};  // Bit_Extender bit_extender_6
  assign bit_extender_7_out = {{3{comparator_7_eq}}, comparator_7_eq};  // Bit_Extender bit_extender_7
  assign bit_extender_8_out = {{3{comparator_8_eq}}, comparator_8_eq};  // Bit_Extender bit_extender_8
  assign bit_extender_9_out = {{3{comparator_9_eq}}, comparator_9_eq};  // Bit_Extender bit_extender_9
  assign bit_extender_10_out = {{3{comparator_10_eq}}, comparator_10_eq};  // Bit_Extender bit_extender_10
  assign bit_extender_11_out = {{3{comparator_11_eq}}, comparator_11_eq};  // Bit_Extender bit_extender_11
  assign bit_extender_12_out = {{3{comparator_12_eq}}, comparator_12_eq};  // Bit_Extender bit_extender_12
  assign bit_extender_13_out = {{3{comparator_13_eq}}, comparator_13_eq};  // Bit_Extender bit_extender_13
  Register #(.width(32)) register_4 (.D(multiplexer_1_out), .en(1'b1), .clk(CLOCK), .Q(write_reg));  // open: clr
  Register #(.width(32)) register_5 (.D(PROGRAM_COUNTER), .en(1'b1), .clk(CLOCK), .Q(PROGRAM_COUNTER_EX));  // open: clr
  assign and_1_out = bit_extender_1_out & 4'b1011;  // AND_Gate and_1, 4 bits wide
  assign and_2_out = bit_extender_2_out & 4'b0000;  // AND_Gate and_2, 4 bits wide
  assign and_3_out = bit_extender_3_out & 4'b1010;  // AND_Gate and_3, 4 bits wide
  assign and_4_out = bit_extender_4_out & 4'b1100;  // AND_Gate and_4, 4 bits wide
  assign and_5_out = bit_extender_5_out & 4'b0110;  // AND_Gate and_5, 4 bits wide
  assign and_6_out = bit_extender_6_out & 4'b1110;  // AND_Gate and_6, 4 bits wide
  assign and_7_out = bit_extender_7_out & 4'b0111;  // AND_Gate and_7, 4 bits wide
  assign and_8_out = bit_extender_8_out & 4'b0011;  // AND_Gate and_8, 4 bits wide
  assign and_9_out = bit_extender_9_out & 4'b1000;  // AND_Gate and_9, 4 bits wide
  assign and_10_out = bit_extender_10_out & 4'b0100;  // AND_Gate and_10, 4 bits wide
  assign and_11_out = bit_extender_11_out & 4'b0010;  // AND_Gate and_11, 4 bits wide
  assign and_12_out = bit_extender_12_out & 4'b1001;  // AND_Gate and_12, 4 bits wide
  assign and_13_out = bit_extender_13_out & 4'b0001;  // AND_Gate and_13, 4 bits wide
  assign ALUSelR = and_1_out | and_2_out | and_3_out | and_4_out | and_5_out | and_6_out | and_7_out | and_8_out | and_9_out | and_10_out | and_11_out | and_12_out | and_13_out;  // OR_Gate or_1, 4 bits wide
  Comparator #(.width(32)) comparator_14 (.a(rs1_output), .b(rs2_output), .eq(beq_sign));  // open: gt, lt
  Comparator #(.width(32)) comparator_15 (.a(rs1_output), .b(rs2_output), .lt(blt_sign));  // open: gt, eq
  Comparator #(.width(32), .mode("unsigned")) comparator_16 (
    .a(rs1_output), .b(rs2_output), .lt(bltu_sign));  // open: gt, eq
  not not_1 (bne_sign, comparator_17_eq);
  Comparator #(.width(32)) comparator_17 (.a(rs1_output), .b(rs2_output), .eq(comparator_17_eq));  // open: gt, lt
  Comparator #(.width(3)) comparator_18 (.a(funct3), .b(3'b000), .eq(comparator_18_eq));  // open: gt, lt
  Comparator #(.width(3)) comparator_19 (.a(funct3), .b(3'b001), .eq(comparator_19_eq));  // open: gt, lt
  Comparator #(.width(3)) comparator_20 (.a(funct3), .b(3'b010), .eq(comparator_20_eq));  // open: gt, lt
  Comparator #(.width(3)) comparator_21 (.a(funct3), .b(3'b100), .eq(comparator_21_eq));  // open: gt, lt
  Comparator #(.width(3)) comparator_22 (.a(funct3), .b(3'b101), .eq(comparator_22_eq));  // open: gt, lt
  Comparator #(.width(4)) comparator_23 (.a({funct3, funct7[5]}), .b(4'b1011), .eq(comparator_23_eq));  // open: gt, lt
  Comparator #(.width(3)) comparator_24 (.a(funct3), .b(3'b110), .eq(comparator_24_eq));  // open: gt, lt
  Comparator #(.width(3)) comparator_25 (.a(funct3), .b(3'b111), .eq(comparator_25_eq));  // open: gt, lt
  Register #(.width(1)) register_6 (.D(PC_Sel), .en(1'b1), .clk(CLOCK), .Q(PC_Sel_tmp));  // open: clr
  Multiplexer #(.width(32), .enable("false")) multiplexer_2 (
    .in0(INSTRUCTION), .in1(32'h13), .out({funct7, INSREUCTION_USE[24:15], funct3, INSREUCTION_USE[11:0]}),
    .sel(PC_Sel_tmp));
  assign bit_extender_14_out = {{3{comparator_18_eq}}, comparator_18_eq};  // Bit_Extender bit_extender_14
  assign bit_extender_15_out = {{3{comparator_19_eq}}, comparator_19_eq};  // Bit_Extender bit_extender_15
  assign bit_extender_16_out = {{3{comparator_20_eq}}, comparator_20_eq};  // Bit_Extender bit_extender_16
  assign bit_extender_17_out = {{3{comparator_21_eq}}, comparator_21_eq};  // Bit_Extender bit_extender_17
  assign bit_extender_18_out = {{3{comparator_22_eq}}, comparator_22_eq};  // Bit_Extender bit_extender_18
  assign bit_extender_19_out = {{3{comparator_23_eq}}, comparator_23_eq};  // Bit_Extender bit_extender_19
  assign bit_extender_20_out = {{3{comparator_24_eq}}, comparator_24_eq};  // Bit_Extender bit_extender_20
  assign bit_extender_21_out = {{3{comparator_25_eq}}, comparator_25_eq};  // Bit_Extender bit_extender_21
  Multiplexer #(.width(32), .enable("false")) multiplexer_3 (
    .in0(PROGRAM_COUNTER), .in1(PROGRAM_COUNTER_EX), .out(multiplexer_3_out), .sel(PC_Sel_tmp));
  Multiplexer #(.width(32), .enable("false")) multiplexer_4 (
    .in0(PROGRAM_COUNTER), .in1(PROGRAM_COUNTER_EX), .out(multiplexer_4_out), .sel(PC_Sel_tmp));
  assign and_14_out = bit_extender_14_out & 4'b0000;  // AND_Gate and_14, 4 bits wide
  assign and_15_out = bit_extender_15_out & 4'b0110;  // AND_Gate and_15, 4 bits wide
  assign and_16_out = bit_extender_16_out & 4'b0111;  // AND_Gate and_16, 4 bits wide
  assign and_17_out = bit_extender_17_out & 4'b0011;  // AND_Gate and_17, 4 bits wide
  assign and_18_out = bit_extender_18_out & 4'b0100;  // AND_Gate and_18, 4 bits wide
  assign and_19_out = bit_extender_19_out & 4'b0101;  // AND_Gate and_19, 4 bits wide
  assign and_20_out = bit_extender_20_out & 4'b0010;  // AND_Gate and_20, 4 bits wide
  assign and_21_out = bit_extender_21_out & 4'b0001;  // AND_Gate and_21, 4 bits wide
  regfile_main RegFile (
    .rs2(INSREUCTION_USE[24:20]), .rd(rd_IF), .Read_Data_1(rs1_output), .Read_Data_2(rs2_output), .ra(ra),
    .sp(sp), .t0(t0), .t1(t1), .t2(t2), .s0(s0), .s1(s1), .a0(a0), .rs1(INSREUCTION_USE[19:15]),
    .Write_Data(write_reg), .RegWEn(RegWEn_IF), .clk(CLOCK));
  Adder #(.width(32)) adder_1 (.a(multiplexer_3_out), .b(32'h4), .out(adder_1_out));  // open: cin, cout
  Adder #(.width(32)) adder_2 (.a(multiplexer_4_out), .b(immi_USE), .out(adder_2_out));  // open: cin, cout
  assign ALUSelI = and_14_out | and_15_out | and_16_out | and_17_out | and_18_out | and_19_out | and_20_out | and_21_out;  // OR_Gate or_2, 4 bits wide
  Multiplexer #(.width(32), .enable("false")) multiplexer_5 (
    .in0(adder_1_out), .in1(adder_2_out), .out(PC_Result), .sel(PC_Sel_tmp));
  Comparator #(.width(3)) comparator_26 (.a(funct3), .b(3'b000), .eq(comparator_26_eq));  // open: gt, lt
  Comparator #(.width(3)) comparator_27 (.a(funct3), .b(3'b100), .eq(comparator_27_eq));  // open: gt, lt
  Comparator #(.width(3)) comparator_28 (.a(funct3), .b(3'b110), .eq(comparator_28_eq));  // open: gt, lt
  Comparator #(.width(3)) comparator_29 (.a(funct3), .b(3'b001), .eq(comparator_29_eq));  // open: gt, lt
  and and_22 (and_22_out, comparator_26_eq, beq_sign);
  and and_23 (and_23_out, comparator_27_eq, blt_sign);
  and and_24 (and_24_out, comparator_28_eq, bltu_sign);
  and and_25 (and_25_out, comparator_29_eq, bne_sign);
  or or_3 (or_3_out, and_22_out, and_23_out, and_24_out, and_25_out);
  Comparator #(.width(7)) comparator_30 (
    .a(INSREUCTION_USE[6:0]), .b(7'b1100011), .eq(comparator_30_eq));  // open: gt, lt
  Comparator #(.width(5)) comparator_31 (.a(INSREUCTION_USE[24:20]), .b(rd_IF), .eq(comparator_31_eq));  // open: gt, lt
  and and_26 (PC_Sel, comparator_30_eq, or_3_out);
  Comparator #(.width(5)) comparator_32 (.a(INSREUCTION_USE[19:15]), .b(rd_IF), .eq(comparator_32_eq));  // open: gt, lt
  Multiplexer #(.width(32), .enable("false")) multiplexer_6 (
    .in0(rs2_output), .in1(write_reg), .out(multiplexer_6_out), .sel(comparator_31_eq));
  Multiplexer #(.width(32), .enable("false")) multiplexer_7 (
    .in0(rs1_output), .in1(write_reg), .out(multiplexer_7_out), .sel(comparator_32_eq));
  Multiplexer #(.width(32), .enable("false")) multiplexer_8 (
    .in0(immi), .in1(multiplexer_6_out), .out(multiplexer_8_out), .sel(ALUB));
  alu Arithmetic_Logic_Unit (.ALUSel(ALUSel), .B(multiplexer_8_out), .A(multiplexer_7_out), .Result(alu_result));
  Comparator #(.width(7)) comparator_33 (
    .a(INSREUCTION_USE[6:0]), .b(7'b0110011), .eq(comparator_33_eq));  // open: gt, lt
  Comparator #(.width(7)) comparator_34 (
    .a(INSREUCTION_USE[6:0]), .b(7'b0010011), .eq(comparator_34_eq));  // open: gt, lt
  Comparator #(.width(7)) comparator_35 (
    .a(INSREUCTION_USE[6:0]), .b(7'b0000011), .eq(comparator_35_eq));  // open: gt, lt
  Comparator #(.width(7)) comparator_36 (
    .a(INSREUCTION_USE[6:0]), .b(7'b0110111), .eq(comparator_36_eq));  // open: gt, lt
  Comparator #(.width(7)) comparator_37 (
    .a(INSREUCTION_USE[6:0]), .b(7'b0100011), .eq(comparator_37_eq));  // open: gt, lt
  Comparator #(.width(7)) comparator_38 (
    .a(INSREUCTION_USE[6:0]), .b(7'b0100011), .eq(comparator_38_eq));  // open: gt, lt
  Comparator #(.width(7)) comparator_39 (
    .a(INSREUCTION_USE[6:0]), .b(7'b0110011), .eq(comparator_39_eq));  // open: gt, lt
  Comparator #(.width(7)) comparator_40 (
    .a(INSREUCTION_USE[6:0]), .b(7'b0010011), .eq(comparator_40_eq));  // open: gt, lt
  Comparator #(.width(7)) comparator_41 (
    .a(INSREUCTION_USE[6:0]), .b(7'b0000011), .eq(comparator_41_eq));  // open: gt, lt
  Comparator #(.width(7)) comparator_42 (
    .a(INSREUCTION_USE[6:0]), .b(7'b0100011), .eq(comparator_42_eq));  // open: gt, lt
  Comparator #(.width(7)) comparator_43 (
    .a(INSREUCTION_USE[6:0]), .b(7'b0110011), .eq(comparator_43_eq));  // open: gt, lt
  Comparator #(.width(7)) comparator_44 (
    .a(INSREUCTION_USE[6:0]), .b(7'b0010011), .eq(comparator_44_eq));  // open: gt, lt
  Comparator #(.width(7)) comparator_45 (
    .a(INSREUCTION_USE[6:0]), .b(7'b0000011), .eq(comparator_45_eq));  // open: gt, lt
  assign bit_extender_22_out = {{3{comparator_43_eq}}, comparator_43_eq};  // Bit_Extender bit_extender_22
  assign bit_extender_23_out = {{3{comparator_44_eq}}, comparator_44_eq};  // Bit_Extender bit_extender_23
  and and_27 (and_27_out, comparator_45_eq, 1'b1);
  and and_28 (and_28_out, comparator_33_eq, 1'b1);
  and and_29 (and_29_out, comparator_34_eq, 1'b1);
  and and_30 (and_30_out, comparator_35_eq, 1'b1);
  and and_31 (and_31_out, comparator_36_eq, 1'b1);
  and and_32 (and_32_out, comparator_37_eq, 1'b0);
  and and_33 (and_33_out, comparator_38_eq, 1'b1);
  and and_34 (and_34_out, comparator_39_eq, 1'b1);
  and and_35 (and_35_out, comparator_40_eq, 1'b0);
  and and_36 (and_36_out, comparator_41_eq, 1'b0);
  and and_37 (and_37_out, comparator_42_eq, 1'b0);
  or or_4 (MemRW, and_33_out, 1'b0);
  or or_5 (ALUB, and_34_out, and_35_out, and_36_out, and_37_out);
  assign and_38_out = bit_extender_22_out & ALUSelR;  // AND_Gate and_38, 4 bits wide
  assign and_39_out = bit_extender_23_out & ALUSelI;  // AND_Gate and_39, 4 bits wide
  or or_6 (store_sel, and_27_out, 1'b0);
  Comparator #(.width(5)) comparator_46 (.a(INSREUCTION_USE[24:20]), .b(rd_IF), .eq(comparator_46_eq));  // open: gt, lt
  or or_7 (RegWEn, and_28_out, and_29_out, and_30_out, and_31_out, and_32_out, 1'b0);
  assign ALUSel = and_38_out | and_39_out | 4'b0000;  // OR_Gate or_8, 4 bits wide
  Multiplexer #(.width(32), .enable("false")) multiplexer_9 (
    .in0(rs2_output), .in1(write_reg), .out(multiplexer_9_out), .sel(comparator_46_eq));
  // mem_main DMEM: pin names not known; wires that end beside it: alu_result, multiplexer_9_out, CLOCK, MemRW, Read_data

  // Other names for the same wires on the sheet: INSREUCTION_USE (some bits) = {funct7, funct3};
  //   SEL[4:0] = {funct3, funct7[5], funct7[0]}; SELI[3:0] = {funct3, funct7[5]}; clk = CLOCK;
  //   opcode[6:0] = INSREUCTION_USE[6:0]; rd[4:0] = INSREUCTION_USE[11:7]; rs1[4:0] = INSREUCTION_USE[19:15];
  //   rs2[4:0] = INSREUCTION_USE[24:20]

  // Notes on the sheet:
  //   mulhu
  //   add
  //   mul
  //   sub
  //   sll
  //   mulh
  //   slt
  //   xor
  //   divu
  //   srl
  //   or
  //   remu
  //   and
  //   Output
  //   R型
  //   IMEM (do **NOT** move this)
  //   Inputs
  //   beq
  //   blt
  //   bltu
  //   bne
  //   addi
  //   slli
  //   slti
  //   xori
  //   srli
  //   srai
  //   ori
  //   andi
  //   I型
  //   Inputs/Outputs for testing. Do **NOT** move these.
  //   beq
  //   blt
  //   bltu
  //   bne
endmodule

module imme (
  input  [31:0] in_1,
  output [31:0] out_2
);

  wire [31:11] I, S;
  wire [31:12] SB;
  wire [31:20] UJ;

  Multiplexer #(.width(21), .enable("false")) multiplexer_1 (
    .in0({21{1'b0}}), .in1({21{1'b1}}), .out(I), .sel(in_1[31]));
  Multiplexer #(.width(21), .enable("false")) multiplexer_2 (
    .in0({21{1'b0}}), .in1({21{1'b1}}), .out(S), .sel(in_1[31]));
  Multiplexer #(.width(20), .enable("false")) multiplexer_3 (
    .in0({20{1'b0}}), .in1({20{1'b1}}), .out(SB), .sel(in_1[31]));
  Multiplexer #(.width(12), .enable("false")) multiplexer_4 (
    .in0({12{1'b0}}), .in1({12{1'b1}}), .out(UJ), .sel(in_1[31]));
  Multiplexer #(.select(3), .width(32), .enable("false")) multiplexer_5 (
    .in0({I, in_1[30:20]}), .in1({S, in_1[30:25], in_1[11:7]}),
    .in3({SB, in_1[7], in_1[30:25], in_1[11:8], 1'b0}), .in5({in_1[31:12], {12{1'b0}}}),
    .in7({UJ, in_1[19:12], in_1[20], in_1[30:21], 1'b0}), .out(out_2), .sel({in_1[2], in_1[6:5]}));  // open: in2, in4, in6

  // Other names for the same wires on the sheet: INSTRUCTION[31:0] = in_1; immi[31:0] = out_2;
  //   S[10:0] = {in_1[30:25], in_1[11:7]}; SB[11:1] = {in_1[7], in_1[30:25], in_1[11:8]}; U[31:12] = in_1[31:12];
  //   I[10:0] = in_1[30:20]; UJ[19:1] = {in_1[19:12], in_1[20], in_1[30:21]}

  // Notes on the sheet:
  //   Output
  //   Inputs
endmodule
